# Fritzing sketch ESP32_RFM95W_BME280 (saved by Fritzing 0.9.6b)
breadboards: 1

parts:
  M1 = DOIT Esp32 DevKit v1 (30 pins long, 11 pins width) [part_number=ESP32S-PIN30]
  RFM95W1 = RFM95W LoRa Module
  Componente1 = BME280 Breakout

nets:
  3V3: M1.3V3, RFM95W1.13_3.3V, Componente1.3.3V
  GND: M1.GND, RFM95W1.1_GND, Componente1.GND
  N1: M1.D5, RFM95W1.5_NSS_(CS)
  N2: M1.D18, RFM95W1.4_SCK
  N3: M1.D19, RFM95W1.2_MISO
  N4: M1.D21, Componente1.SDI/SDA
  N5: M1.D22, Componente1.SCK/SCL
  N6: M1.D23, RFM95W1.3_MOSI
  N7: M1.D33, RFM95W1.15_DIO1
  N8: M1.D26, RFM95W1.14_DIO0
  N9: M1.D14, RFM95W1.6_RESET

notes:
  ESP32
  3.3v
  MISO (GPIO19)
  MOSI (GPIO23)
  SCK (GPIO18)
  NSS (GPIO5)
  RST (GPIO14)
  GND
  DIO0(GPIO26)
  DIO1(GPIO33)
  RFM95W
  30 pins
  SDA (GPIO21)
  SCL (GPIO22)
  BME280

custom parts:
  DOIT Esp32 DevKit v1 (30 pins long, 11 pins width): The DOIT Esp32 DevKit v1 is one of the development board created by DOIT to evaluate the ESP-WROOM-32 module. It is based on the ESP32 microcontroller that boasts Wifi, Bluetooth, Ethernet and Low Power support all in a single chip. (vanepp) made breadboard work, adjusted pin numbering and labels and reduced size of schematic and cleaned up pcb. This chip is 30pins long (2 x15) and 11 pins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
  RFM95W LoRa Module: RF Transceiver by Hope RF. Well supported Arduino libraries are available. This Low Power Long Range Transceiver Module for the frequencies 868MHz and 915MHz and it is also available in other versions.
